# Fritzing sketch tutorialpiano (1) (saved by Fritzing 0.9.3b)
breadboards: 6

parts:
  S1 = Pushbutton [package="[THT]"]
  S2 = Pushbutton [package="[THT]"]
  S3 = Pushbutton [package="[THT]"]
  S4 = Pushbutton [package="[THT]"]
  S5 = Pushbutton [package="[THT]"]
  S6 = Pushbutton [package="[THT]"]
  S7 = Pushbutton [package="[THT]"]
  S8 = Pushbutton [package="[THT]"]
  S9 = Pushbutton [package="[THT]"]
  S10 = Pushbutton [package="[THT]"]
  S11 = Pushbutton [package="[THT]"]
  S12 = Pushbutton [package="[THT]"]
  R1 = Resistor [tolerance=±5% resistance=220 package=THT]
  R2 = Resistor [tolerance=±5% resistance=220 package=THT]
  R3 = Resistor [tolerance=±5% resistance=220 package=THT]
  R4 = Resistor [tolerance=±5% resistance=220 package=THT]
  R5 = Resistor [tolerance=±5% resistance=220 package=THT]
  R6 = Resistor [tolerance=±5% resistance=220 package=THT]
  R7 = Resistor [tolerance=±5% resistance=220 package=THT]
  R8 = Resistor [tolerance=±5% resistance=220 package=THT]
  R9 = Resistor [tolerance=±5% resistance=220 package=THT]
  R10 = Resistor [tolerance=±5% resistance=220 package=THT]
  R11 = Resistor [tolerance=±5% resistance=220 package=THT]
  R12 = Resistor [tolerance=±5% resistance=220 package=THT]
  Q1 = NPN-Transistor [package="TO92 [THT]"]
  Q2 = NPN-Transistor [package="TO92 [THT]"]
  Q3 = NPN-Transistor [package="TO92 [THT]"]
  Q4 = NPN-Transistor [package="TO92 [THT]"]
  Q5 = NPN-Transistor [package="TO92 [THT]"]
  Q6 = NPN-Transistor [package="TO92 [THT]"]
  Q7 = NPN-Transistor [package="TO92 [THT]"]
  Q8 = NPN-Transistor [package="TO92 [THT]"]
  Q9 = NPN-Transistor [package="TO92 [THT]"]
  Q10 = NPN-Transistor [package="TO92 [THT]"]
  Q11 = NPN-Transistor [package="TO92 [THT]"]
  Q12 = NPN-Transistor [package="TO92 [THT]"]
  LED1 = LED - 5mm [color="Red (633nm)" package="5 mm [THT]"]
  LED2 = LED - 5mm [color="Red (633nm)" package="5 mm [THT]"]
  LED3 = LED - 5mm [color="Red (633nm)" package="5 mm [THT]"]
  LED4 = LED - 5mm [color="Red (633nm)" package="5 mm [THT]"]
  LED5 = LED - 5mm [color="Red (633nm)" package="5 mm [THT]"]
  LED6 = LED - 5mm [color="Red (633nm)" package="5 mm [THT]"]
  LED7 = LED - 5mm [color="Red (633nm)" package="5 mm [THT]"]
  LED8 = LED - 5mm [color="Red (633nm)" package="5 mm [THT]"]
  LED9 = LED - 5mm [color="Red (633nm)" package="5 mm [THT]"]
  LED10 = LED - 5mm [color="Red (633nm)" package="5 mm [THT]"]
  LED11 = LED - 5mm [color="Red (633nm)" package="5 mm [THT]"]
  LED12 = LED - 5mm [color="Red (633nm)" package="5 mm [THT]"]
  IC1 = Eleduino T-Cobbler [chip_label=IC package=Custom]  # not connected

nets:
  N1: S1.Pin_1, S1.Pin_2, S1.Pin_3, S1.Pin_4, S2.Pin_1, S2.Pin_2, S2.Pin_3, S2.Pin_4, S3.Pin_1, S3.Pin_2, S3.Pin_3, S3.Pin_4, S4.Pin_1, S4.Pin_2, S4.Pin_3, S4.Pin_4, S5.Pin_1, S5.Pin_2, S5.Pin_3, S5.Pin_4, S6.Pin_1, S6.Pin_2, S6.Pin_3, S6.Pin_4, S7.Pin_1, S7.Pin_2, S7.Pin_3, S7.Pin_4, S9.Pin_1, S9.Pin_2, S10.Pin_3, S10.Pin_4, S11.Pin_3, S11.Pin_4, S12.Pin_1, S12.Pin_2
  N2: S8.Pin_3, S8.Pin_4, R9.Pin_1, R11.Pin_1, R12.Pin_0
  N3: S9.Pin_3, S9.Pin_4
  N4: S12.Pin_3, S12.Pin_4
  N5: R1.Pin_0, R2.Pin_0, R3.Pin_0, R4.Pin_0, R5.Pin_0, R6.Pin_0, R7.Pin_0, R8.Pin_0, R10.Pin_0
  N6: R1.Pin_1, LED12.cathode
  N7: R2.Pin_1, LED9.cathode
  N8: R3.Pin_1, LED6.cathode
  N9: R4.Pin_1, LED8.cathode
  N10: R5.Pin_1, LED7.cathode
  N11: R6.Pin_1, LED10.cathode
  N12: R7.Pin_1, LED11.anode
  N13: R8.Pin_1, LED5.cathode
  N14: R9.Pin_0, LED4.cathode
  N15: R10.Pin_1, LED3.cathode
  N16: R11.Pin_0, LED1.anode
  N17: Q1.E, LED3.anode
  N18: Q1.C, Q2.C, Q3.C, Q4.C, Q5.C, Q6.C, Q7.C, Q8.C, Q9.C, Q10.C, Q11.C, Q12.C
  N19: Q2.E, LED4.anode
  N20: Q3.E, LED5.anode
  N21: Q4.E, LED10.anode
  N22: Q5.E, LED11.cathode
  N23: Q6.E, LED8.anode
  N24: Q7.E, LED9.anode
  N25: Q8.E, LED7.anode
  N26: Q10.E, LED6.anode
  N27: Q11.E, LED1.cathode
  N28: Q12.E, LED2.cathode

custom parts:
  Eleduino T-Cobbler: The Alvar and Hurriks T-Cobbler for use with the Raspberry Pi v2 Model B or v3 for bringout out the GPIO pins to a breadboard.
